// Logisim project Hack Derivative.circ as structural Verilog: 10 circuits, main circuit Or16Way
module Or16Way (
  input  [15:0] in_1,
  output out_2
);

  or or_1 (out_2, in_1[0], in_1[1], in_1[2], in_1[3], in_1[4], in_1[5], in_1[6], in_1[7], in_1[8], in_1[9], in_1[10], in_1[11], in_1[12], in_1[13], in_1[14], in_1[15]);
endmodule

module ALU (
  input  [15:0] X,
  input  Zx,
  input  Nx,
  input  [15:0] Y,
  input  Zy,
  input  Ny,
  input  No,
  input  F,
  input  ShR,
  output [15:0] Out,
  output Ng,
  output Zr
);

  wire adder_1_cout, or16way_1_out_2;
  wire [15:0] adder_1_out, and_1_out, multiplexer_1_out, multiplexer_2_out, multiplexer_3_out,
       multiplexer_4_out, multiplexer_5_out, multiplexer_6_out, not_1_out, not_2_out, not_3_out,
       shifter_1_out;

  Multiplexer #(.width(16), .enable("false")) multiplexer_1 (
    .in0(X), .in1({16{1'b0}}), .out(multiplexer_1_out), .sel(Zx));
  Multiplexer #(.width(16), .enable("false")) multiplexer_2 (
    .in0(Y), .in1({16{1'b0}}), .out(multiplexer_2_out), .sel(Zy));
  assign and_1_out = multiplexer_3_out & multiplexer_4_out;  // AND_Gate and_1, 16 bits wide
  Adder #(.width(16)) adder_1 (
    .a(multiplexer_3_out), .b(multiplexer_4_out), .out(adder_1_out), .cin(1'b0), .cout(adder_1_cout));
  Multiplexer #(.width(16), .enable("false")) multiplexer_3 (
    .in0(multiplexer_1_out), .in1(not_1_out), .out(multiplexer_3_out), .sel(Nx));
  assign not_1_out = ~multiplexer_1_out;  // NOT_Gate not_1, 16 bits wide
  Multiplexer #(.width(16), .enable("false")) multiplexer_4 (
    .in0(multiplexer_2_out), .in1(not_2_out), .out(multiplexer_4_out), .sel(Ny));
  assign not_2_out = ~multiplexer_2_out;  // NOT_Gate not_2, 16 bits wide
  Multiplexer #(.width(16), .enable("false")) multiplexer_5 (
    .in0(and_1_out), .in1(adder_1_out), .out(multiplexer_5_out), .sel(F));
  Multiplexer #(.width(16), .enable("false")) multiplexer_6 (
    .in0(multiplexer_5_out), .in1(not_3_out), .out(multiplexer_6_out), .sel(No));
  assign not_3_out = ~multiplexer_5_out;  // NOT_Gate not_3, 16 bits wide
  Shifter #(.width(16), .shift("lr")) shifter_1 (.in(multiplexer_6_out), .\dist (4'b0001), .out(shifter_1_out));
  or or_1 (Ng, multiplexer_6_out[15], adder_1_cout);
  not not_4 (Zr, or16way_1_out_2);
  Or16Way or16way_1 (.in_1(multiplexer_6_out), .out_2(or16way_1_out_2));
  Multiplexer #(.width(16), .enable("false")) multiplexer_7 (
    .in0(multiplexer_6_out), .in1(shifter_1_out), .out(Out), .sel(ShR));
endmodule

module Registers (
  input  [2:0] X_Select,
  input  [15:0] Outbus,
  input  [2:0] Out_Select,
  input  [2:0] Y_Select,
  input  CLK,
  input  Rst,
  output [15:0] PC,
  output [15:0] Xbus,
  output [15:0] Ybus,
  output [15:0] Mem,
  output [15:0] Instruction
);

  wire decoder_1_out0, decoder_1_out1, decoder_1_out2, decoder_1_out3, decoder_1_out4, decoder_1_out5,
       decoder_1_out6, decoder_1_out7;
  wire [15:0] A_q, B_q, C_q, D_q, demultiplexer_1_out0, demultiplexer_1_out1, demultiplexer_1_out2,
       demultiplexer_1_out3, demultiplexer_1_out4, demultiplexer_1_out5, demultiplexer_1_out6,
       demultiplexer_1_out7, SP_q;

  Demultiplexer #(.select(3), .width(16), .enable("false")) demultiplexer_1 (
    .out0(demultiplexer_1_out0), .out1(demultiplexer_1_out1), .out2(demultiplexer_1_out2),
    .out3(demultiplexer_1_out3), .out4(demultiplexer_1_out4), .out5(demultiplexer_1_out5),
    .out6(demultiplexer_1_out6), .out7(demultiplexer_1_out7), .in(Outbus), .sel(Out_Select));
  Decoder #(.select(3), .disabled(0), .enable("false")) decoder_1 (
    .out0(decoder_1_out0), .out1(decoder_1_out1), .out2(decoder_1_out2), .out3(decoder_1_out3),
    .out4(decoder_1_out4), .out5(decoder_1_out5), .out6(decoder_1_out6), .out7(decoder_1_out7),
    .sel(Out_Select));
  Register #(.width(16)) u_PC (.D(demultiplexer_1_out0), .en(decoder_1_out0), .Q(PC), .clk(CLK), .clr(Rst));
  Register #(.width(16)) IR (.D(demultiplexer_1_out1), .en(decoder_1_out1), .Q(Instruction), .clk(CLK), .clr(Rst));
  Register #(.width(16)) SP (.D(demultiplexer_1_out2), .en(decoder_1_out2), .Q(SP_q), .clk(CLK), .clr(Rst));
  Register #(.width(16)) u_Mem (.D(demultiplexer_1_out3), .en(decoder_1_out3), .Q(Mem), .clk(CLK), .clr(Rst));
  Register #(.width(16)) A (.D(demultiplexer_1_out4), .en(decoder_1_out4), .Q(A_q), .clk(CLK), .clr(Rst));
  Register #(.width(16)) B (.D(demultiplexer_1_out5), .en(decoder_1_out5), .Q(B_q), .clk(CLK), .clr(Rst));
  Register #(.width(16)) C (.D(demultiplexer_1_out6), .en(decoder_1_out6), .Q(C_q), .clk(CLK), .clr(Rst));
  Register #(.width(16)) D (.D(demultiplexer_1_out7), .en(decoder_1_out7), .Q(D_q), .clk(CLK), .clr(Rst));
  Multiplexer #(.select(3), .width(16), .enable("false")) multiplexer_1 (
    .in0(PC), .in1(Instruction), .in2(SP_q), .in3(Mem), .in4(A_q), .in5(B_q), .in6(C_q), .in7(D_q),
    .out(Xbus), .sel(X_Select));
  Multiplexer #(.select(3), .width(16), .enable("false")) multiplexer_2 (
    .in0(PC), .in1(Instruction), .in2(SP_q), .in3(Mem), .in4(A_q), .in5(B_q), .in6(C_q), .in7(D_q),
    .out(Ybus), .sel(Y_Select));
endmodule

module Instruction_Decoder (
  input  [15:0] In,
  output [2:0] OutSel,
  output Zx,
  output [2:0] YSel,
  output [2:0] XSel,
  output Nx,
  output [15:0] To_Direct_Unit,
  output Zy,
  output Load,
  output Ny,
  output Store,
  output f,
  output BRx_y,
  output BRx_y_2,
  output BRx__y,
  output No,
  output JumpMem,
  output Fault,
  output Shift_Right
);

  wire decoder_1_out0, decoder_1_out1, decoder_1_out2, decoder_1_out4, decoder_1_out5, decoder_1_out6,
       decoder_1_out7, decoder_1_out8, decoder_1_out9, decoder_1_out11, or_1_out, or_3_out, X_Instruction,
       X_or_Store;
  wire [4:0] multiplexer_1_out;

  or or_1 (or_1_out, Store, Shift_Right);
  or or_2 (X_or_Store, X_Instruction, or_1_out);
  Decoder #(.select(5), .disabled(0), .enable("false")) decoder_1 (
    .out0(decoder_1_out0), .out1(decoder_1_out1), .out2(decoder_1_out2), .out3(X_Instruction),
    .out4(decoder_1_out4), .out5(decoder_1_out5), .out6(decoder_1_out6), .out7(decoder_1_out7),
    .out8(decoder_1_out8), .out9(decoder_1_out9), .out11(decoder_1_out11), .out12(Load), .out13(Store),
    .out14(BRx_y), .out15(BRx_y_2), .out16(BRx__y), .out17(JumpMem), .out18(Fault), .out19(Shift_Right),
    .sel(multiplexer_1_out));  // open: out10, out20, out21, out22, out23, out24, out25, out26, out27, out28, out29, out30, out31
  Multiplexer #(.width(5), .enable("false")) multiplexer_1 (
    .in0(In[13:9]), .in1({5{1'b0}}), .out(multiplexer_1_out), .sel(In[15]));
  or or_3 (or_3_out, decoder_1_out9, BRx_y, BRx_y_2, BRx__y);
  or or_4 (Zx, decoder_1_out1, decoder_1_out2, decoder_1_out0);
  or or_5 (Nx, decoder_1_out1, or_3_out, decoder_1_out11, decoder_1_out2, decoder_1_out6);
  or or_6 (Zy, decoder_1_out4, decoder_1_out0, decoder_1_out1, decoder_1_out2, X_or_Store, decoder_1_out5, decoder_1_out7, decoder_1_out6, decoder_1_out6, decoder_1_out6);
  or or_7 (Ny, decoder_1_out1, X_or_Store, decoder_1_out4, decoder_1_out5, decoder_1_out5, decoder_1_out6, decoder_1_out7);
  or or_8 (f, decoder_1_out0, decoder_1_out1, decoder_1_out2, decoder_1_out5, decoder_1_out6, decoder_1_out7, decoder_1_out8, or_3_out);
  or or_9 (No, decoder_1_out1, decoder_1_out4, decoder_1_out5, decoder_1_out6, or_3_out, decoder_1_out11);

  assign OutSel = In[2:0];
  assign To_Direct_Unit = In;
  assign XSel = In[8:6];
  assign YSel = In[5:3];
endmodule

module Set_Direct_unit (
  input  [15:0] SetIn,
  input  [15:0] StdIn,
  input  [2:0] in_3,
  output [15:0] Result,
  output [2:0] out_5
);

  Multiplexer #(.width(16), .enable("false")) multiplexer_1 (
    .in0(StdIn), .in1({1'b0, SetIn[14:0]}), .out(Result), .sel(SetIn[15]));
  Multiplexer #(.width(3), .enable("false")) multiplexer_2 (.in0(in_3), .in1(3'b011), .out(out_5), .sel(SetIn[15]));
endmodule

module Control_unit (
  input  Clock,
  input  Branch,
  input  RST,
  output Fetch,
  output [15:0] out_5,
  output [15:0] Instruction,
  output Update,
  output Control,
  output Clear_Branch
);

  wire and_1_out, decoder_1_out1, decoder_1_out3, decoder_1_out4, decoder_1_out5, decoder_1_out6,
       decoder_1_out7, not_1_out, or_1_out;
  wire [2:0] counter_1_q;
  wire [15:0] multiplexer_1_out;

  Counter #(.width(3), .max('h7)) counter_1 (
    .count(1'b1), .Q(counter_1_q), .clk(Clock), .clr(or_1_out));  // open: load, D, carry
  or or_1 (or_1_out, RST, and_1_out);
  and and_1 (and_1_out, decoder_1_out6, not_1_out);
  Decoder #(.select(3), .disabled(0), .enable("false")) decoder_1 (
    .out0(Clear_Branch), .out1(decoder_1_out1), .out3(decoder_1_out3), .out4(decoder_1_out4),
    .out5(decoder_1_out5), .out6(decoder_1_out6), .out7(decoder_1_out7), .sel(counter_1_q));  // open: out2
  not not_1 (not_1_out, Branch);
  nor nor_1 (Fetch, decoder_1_out4, decoder_1_out5);
  or or_2 (Update, decoder_1_out1, decoder_1_out3, decoder_1_out5, decoder_1_out7);
  nor nor_2 (Control, decoder_1_out4, decoder_1_out5);
  Multiplexer #(.width(16), .enable("false")) multiplexer_1 (
    .in0(16'h1), .in1(16'h6c0), .out(multiplexer_1_out), .sel(Branch));
  Multiplexer #(.select(3), .width(16), .enable("false")) multiplexer_2 (
    .in0(16'h1801), .in1(16'h1801), .in2(16'hc00), .in3(16'hc00), .in4({16{1'b0}}), .in5({16{1'b0}}),
    .in6(multiplexer_1_out), .in7(multiplexer_1_out), .out(Instruction), .sel(counter_1_q));

  assign out_5 = 16'h6c0;
endmodule

module Branch_Unit (
  input  CLK,
  input  Ng,
  input  Zr,
  input  X_Y,
  input  X_Y_2,
  input  X__Y,
  input  Jump,
  input  Clear,
  output Branch
);

  wire and_1_out, and_2_out, and_3_out, d_ff_1_q, d_ff_2_q, or_1_out, or_2_out;

  D_Flip_Flop #(.trigger("high")) d_ff_1 (.clk(CLK), .D(Ng), .Q(d_ff_1_q), .reset(Clear));  // open: Qn, preset, en
  D_Flip_Flop #(.trigger("high")) d_ff_2 (.clk(CLK), .D(Zr), .Q(d_ff_2_q), .reset(Clear));  // open: Qn, preset, en
  or or_1 (or_1_out, d_ff_1_q, d_ff_2_q);
  and and_1 (and_1_out, d_ff_2_q, X_Y);
  and and_2 (and_2_out, d_ff_1_q, X_Y_2);
  and and_3 (and_3_out, or_1_out, X__Y);
  or or_2 (or_2_out, and_2_out, and_1_out, and_3_out, Jump);
  D_Flip_Flop d_ff_3 (.clk(or_2_out), .D(or_2_out), .Q(Branch), .reset(Clear));  // open: Qn, preset, en
endmodule

module TestBed (
  input  [15:0] in_1,
  output [15:0] out_2,
  output Halt
);

  wire alu_1_ng, alu_1_zr, and_1_out, branch_unit_1_branch, button_1_out, clock_1_out,
       control_unit_1_clear_branch, control_unit_1_control, control_unit_1_fetch, control_unit_1_update,
       instruction_decoder_1_brx__y, instruction_decoder_1_brx_y, instruction_decoder_1_brx_y_2,
       instruction_decoder_1_f, instruction_decoder_1_jumpmem, instruction_decoder_1_load,
       instruction_decoder_1_no, instruction_decoder_1_nx, instruction_decoder_1_ny,
       instruction_decoder_1_shift_right, instruction_decoder_1_store, instruction_decoder_1_zx,
       instruction_decoder_1_zy, not_1_out, or_1_out;
  wire [2:0] instruction_decoder_1_outsel, instruction_decoder_1_xsel, instruction_decoder_1_ysel,
       set_direct_unit_1_out_5;
  wire [15:0] control_unit_1_instruction, instruction_decoder_1_to_direct_unit, multiplexer_1_out,
       multiplexer_2_out, multiplexer_3_out, ram_1_data, registers_1_instruction, registers_1_mem,
       registers_1_pc, registers_1_xbus, registers_1_ybus, set_direct_unit_1_result;

  Clock clock_1 (.out(clock_1_out));
  or or_1 (or_1_out, not_1_out, button_1_out);
  and and_1 (and_1_out, clock_1_out, or_1_out);
  Button button_1 (.out(button_1_out));
  Control_unit control_unit_1 (
    .Clock(and_1_out), .Update(control_unit_1_update), .Instruction(control_unit_1_instruction),
    .Control(control_unit_1_control), .Clear_Branch(control_unit_1_clear_branch),
    .Branch(branch_unit_1_branch), .Fetch(control_unit_1_fetch));  // open: out_5, RST
  RAM #(.addrWidth(16), .dataWidth(16), .bus("separate")) ram_1 (
    .addr(multiplexer_2_out), .din(out_2), .data(ram_1_data), .str(instruction_decoder_1_store),
    .clk(control_unit_1_update), .ld(instruction_decoder_1_load));  // open: sel, clr
  Multiplexer #(.width(16), .enable("false")) multiplexer_1 (
    .in0(registers_1_instruction), .in1(control_unit_1_instruction), .out(multiplexer_1_out),
    .sel(control_unit_1_control));
  not not_1 (not_1_out, Halt);
  Multiplexer #(.width(16), .enable("false")) multiplexer_2 (
    .in0(registers_1_mem), .in1(registers_1_pc), .out(multiplexer_2_out), .sel(control_unit_1_fetch));
  Multiplexer #(.width(16), .enable("false")) multiplexer_3 (
    .in0(set_direct_unit_1_result), .in1(ram_1_data), .out(multiplexer_3_out),
    .sel(instruction_decoder_1_load));
  Set_Direct_unit set_direct_unit_1 (
    .SetIn(instruction_decoder_1_to_direct_unit), .StdIn(out_2), .Result(set_direct_unit_1_result),
    .in_3(instruction_decoder_1_outsel), .out_5(set_direct_unit_1_out_5));
  Instruction_Decoder instruction_decoder_1 (
    .In(multiplexer_1_out), .OutSel(instruction_decoder_1_outsel), .Zx(instruction_decoder_1_zx),
    .XSel(instruction_decoder_1_xsel), .YSel(instruction_decoder_1_ysel), .Nx(instruction_decoder_1_nx),
    .Zy(instruction_decoder_1_zy), .Load(instruction_decoder_1_load), .Ny(instruction_decoder_1_ny),
    .Store(instruction_decoder_1_store), .f(instruction_decoder_1_f), .BRx_y(instruction_decoder_1_brx_y),
    .BRx_y_2(instruction_decoder_1_brx_y_2), .BRx__y(instruction_decoder_1_brx__y),
    .No(instruction_decoder_1_no), .JumpMem(instruction_decoder_1_jumpmem),
    .To_Direct_Unit(instruction_decoder_1_to_direct_unit), .Fault(Halt),
    .Shift_Right(instruction_decoder_1_shift_right));
  Registers registers_1 (
    .Outbus(multiplexer_3_out), .Out_Select(set_direct_unit_1_out_5), .CLK(control_unit_1_update),
    .Xbus(registers_1_xbus), .X_Select(instruction_decoder_1_xsel), .Ybus(registers_1_ybus),
    .Y_Select(instruction_decoder_1_ysel), .Mem(registers_1_mem), .Instruction(registers_1_instruction),
    .PC(registers_1_pc));  // open: Rst
  Branch_Unit branch_unit_1 (
    .Ng(alu_1_ng), .Zr(alu_1_zr), .X_Y(instruction_decoder_1_brx_y), .X_Y_2(instruction_decoder_1_brx_y_2),
    .X__Y(instruction_decoder_1_brx__y), .Jump(instruction_decoder_1_jumpmem),
    .Clear(control_unit_1_clear_branch), .Branch(branch_unit_1_branch), .CLK(control_unit_1_update));
  ALU alu_1 (
    .X(registers_1_xbus), .Zx(instruction_decoder_1_zx), .Nx(instruction_decoder_1_nx), .Y(registers_1_ybus),
    .Zy(instruction_decoder_1_zy), .Ny(instruction_decoder_1_ny), .No(instruction_decoder_1_no),
    .F(instruction_decoder_1_f), .Out(out_2), .Ng(alu_1_ng), .Zr(alu_1_zr),
    .ShR(instruction_decoder_1_shift_right));
  // Probe on in_1
endmodule

module CPU (
  input  [15:0] Data_In,
  input  CLK_SRC_In,
  input  Reset,
  output [15:0] RAM_Address,
  output [15:0] Data_Out,
  output Bus_Clock,
  output Load,
  output Store,
  output Halt
);

  wire alu_1_ng, alu_1_zr, and_1_out, branch_unit_1_branch, control_unit_1_clear_branch,
       control_unit_1_control, control_unit_1_fetch, instruction_decoder_1_brx__y,
       instruction_decoder_1_brx_y, instruction_decoder_1_brx_y_2, instruction_decoder_1_f,
       instruction_decoder_1_jumpmem, instruction_decoder_1_no, instruction_decoder_1_nx,
       instruction_decoder_1_ny, instruction_decoder_1_shift_right, instruction_decoder_1_zx,
       instruction_decoder_1_zy, not_1_out, or_1_out;
  wire [2:0] instruction_decoder_1_outsel, instruction_decoder_1_xsel, instruction_decoder_1_ysel,
       set_direct_unit_1_out_5;
  wire [15:0] control_unit_1_instruction, instruction_decoder_1_to_direct_unit, multiplexer_1_out,
       multiplexer_3_out, registers_1_instruction, registers_1_mem, registers_1_pc, registers_1_xbus,
       registers_1_ybus, set_direct_unit_1_result;

  or or_1 (or_1_out, not_1_out, Reset);
  and and_1 (and_1_out, CLK_SRC_In, or_1_out);
  Control_unit control_unit_1 (
    .Clock(and_1_out), .Update(Bus_Clock), .Instruction(control_unit_1_instruction),
    .Control(control_unit_1_control), .Clear_Branch(control_unit_1_clear_branch),
    .Branch(branch_unit_1_branch), .Fetch(control_unit_1_fetch), .RST(Reset));  // open: out_5
  Multiplexer #(.width(16), .enable("false")) multiplexer_1 (
    .in0(registers_1_instruction), .in1(control_unit_1_instruction), .out(multiplexer_1_out),
    .sel(control_unit_1_control));
  Multiplexer #(.width(16), .enable("false")) multiplexer_2 (
    .in0(registers_1_mem), .in1(registers_1_pc), .out(RAM_Address), .sel(control_unit_1_fetch));
  Multiplexer #(.width(16), .enable("false")) multiplexer_3 (
    .in0(set_direct_unit_1_result), .in1(Data_In), .out(multiplexer_3_out), .sel(Load));
  Set_Direct_unit set_direct_unit_1 (
    .SetIn(instruction_decoder_1_to_direct_unit), .StdIn(Data_Out), .Result(set_direct_unit_1_result),
    .in_3(instruction_decoder_1_outsel), .out_5(set_direct_unit_1_out_5));
  not not_1 (not_1_out, Halt);
  Instruction_Decoder instruction_decoder_1 (
    .In(multiplexer_1_out), .OutSel(instruction_decoder_1_outsel), .Zx(instruction_decoder_1_zx),
    .XSel(instruction_decoder_1_xsel), .YSel(instruction_decoder_1_ysel), .Nx(instruction_decoder_1_nx),
    .Zy(instruction_decoder_1_zy), .Load(Load), .Ny(instruction_decoder_1_ny), .Store(Store),
    .f(instruction_decoder_1_f), .BRx_y(instruction_decoder_1_brx_y),
    .BRx_y_2(instruction_decoder_1_brx_y_2), .BRx__y(instruction_decoder_1_brx__y),
    .No(instruction_decoder_1_no), .JumpMem(instruction_decoder_1_jumpmem),
    .To_Direct_Unit(instruction_decoder_1_to_direct_unit), .Fault(Halt),
    .Shift_Right(instruction_decoder_1_shift_right));
  Registers registers_1 (
    .Outbus(multiplexer_3_out), .Out_Select(set_direct_unit_1_out_5), .CLK(Bus_Clock),
    .Xbus(registers_1_xbus), .X_Select(instruction_decoder_1_xsel), .Ybus(registers_1_ybus),
    .Y_Select(instruction_decoder_1_ysel), .Mem(registers_1_mem), .Instruction(registers_1_instruction),
    .PC(registers_1_pc), .Rst(Reset));
  Branch_Unit branch_unit_1 (
    .Ng(alu_1_ng), .Zr(alu_1_zr), .X_Y(instruction_decoder_1_brx_y), .X_Y_2(instruction_decoder_1_brx_y_2),
    .X__Y(instruction_decoder_1_brx__y), .Jump(instruction_decoder_1_jumpmem),
    .Clear(control_unit_1_clear_branch), .Branch(branch_unit_1_branch), .CLK(Bus_Clock));
  ALU alu_1 (
    .X(registers_1_xbus), .Zx(instruction_decoder_1_zx), .Nx(instruction_decoder_1_nx), .Y(registers_1_ybus),
    .Zy(instruction_decoder_1_zy), .Ny(instruction_decoder_1_ny), .No(instruction_decoder_1_no),
    .F(instruction_decoder_1_f), .Out(Data_Out), .Ng(alu_1_ng), .Zr(alu_1_zr),
    .ShR(instruction_decoder_1_shift_right));
endmodule

module Motherboard (
);

  wire button_1_out, clock_1_out, cpu_1_bus_clock, cpu_1_halt, cpu_1_load, cpu_1_store;
  wire [15:0] cpu_1_data_out, cpu_1_ram_address, ram_1_data;

  ROM #(.addrWidth(16), .dataWidth(16)) rom_1 ();  // open: addr, data, sel
  LED led_1 (.in(cpu_1_halt));
  RAM #(.addrWidth(16), .dataWidth(16), .bus("separate")) ram_1 (
    .addr(cpu_1_ram_address), .din(cpu_1_data_out), .data(ram_1_data), .str(cpu_1_store),
    .clk(cpu_1_bus_clock), .ld(cpu_1_load));  // open: sel, clr
  CPU cpu_1 (
    .Data_In(ram_1_data), .CLK_SRC_In(clock_1_out), .Reset(button_1_out), .RAM_Address(cpu_1_ram_address),
    .Data_Out(cpu_1_data_out), .Bus_Clock(cpu_1_bus_clock), .Load(cpu_1_load), .Store(cpu_1_store),
    .Halt(cpu_1_halt));
  Clock clock_1 (.out(clock_1_out));
  Button button_1 (.out(button_1_out));

  // Notes on the sheet:
  //   Reset
endmodule
